// Logisim project ex1.circ as structural Verilog
module Exp1 (
  output SOMA,
  output CARRY_OUT
);

  wire undriven, undriven_2;

  // Probe on undriven_2
  // Probe on undriven
  xor xor_1 (SOMA, undriven_2, undriven);
  and and_1 (CARRY_OUT, undriven_2, undriven);

  // Notes on the sheet:
  //   A0
  //   B0
endmodule
